// Logisim project New Text Document (4).circ as structural Verilog: 2 circuits, main circuit main
module main (
  input  A2,
  input  B2,
  input  A1,
  input  B1,
  input  A0,
  input  B0,
  input  C2,
  input  S2,
  input  S1,
  input  S0,
  output Cin
);

  wire FA1_p5, fa_1_cout;

  FA fa_1 (.A(A2), .B(C2), .Cin(S2), .S(B2), .Cout(fa_1_cout));
  // FA FA1: pin names not known; wires that end beside it: A1, fa_1_cout, S1, B1, FA1_p5
  FA fa_2 (.A(A0), .B(B0), .Cin(S0), .S(FA1_p5), .Cout(Cin));

  // Notes on the sheet:
  //   FA2
  //   FA0
endmodule

module FA (
  input  A,
  input  B,
  input  Cin,
  output S,
  output Cout
);

  wire and_1_out;

  buf or_1 (S, A);  // OR_Gate
  and and_1 (and_1_out, B, Cin);
  buf and_2 (Cout, and_1_out);  // AND_Gate
  // OR_Gate or_2 has open pins: in2=and_1_out, out=open
endmodule
