// Logisim project Rangkaian JK Flip Flop - Logisim.circ as structural Verilog: 1 circuit, main circuit main
module main (
  input  J,
  input  K,
  output Q,
  output Q_prime
);

  wire clock_1_out, nand_1_out, nand_2_out;

  Clock clock_1 (.out(clock_1_out));
  nand nand_1 (nand_1_out, Q_prime, J, clock_1_out);
  nand nand_2 (nand_2_out, clock_1_out, K, Q);
  nand nand_3 (Q, nand_1_out, Q_prime);
  nand nand_4 (Q_prime, Q, nand_2_out);

  // Notes on the sheet:
  //   CLK
  //   NIM: 265150300111021
  //   NAND Gate
  //   NAND Gate
  //   Nama: Muhammad Gilmar Fawwaz Azzahra
  //   Rangkaian JK Flip Flop
  //   NAND Gate
  //   NAND Gate
endmodule
