// Logisim project Rangkaian T Flip Flop - Logisim.circ as structural Verilog: 1 circuit, main circuit main
module main (
  input  T,
  output Q,
  output Q_prime
);

  wire and_1_out, and_2_out, clock_1_out;

  Clock clock_1 (.out(clock_1_out));
  and and_1 (and_1_out, Q_prime, T, clock_1_out);
  and and_2 (and_2_out, clock_1_out, T, Q);
  nor nor_1 (Q, and_1_out, Q_prime);
  nor nor_2 (Q_prime, Q, and_2_out);

  // Notes on the sheet:
  //   CLK
  //   Nama: Muhammad Gilmar Fawwaz Azzahra
  //   NIM: 265150300111021
  //   AND Gate
  //   AND Gate
  //   Rangkaian T Flip Flop
  //   XOR Gate
  //   XOR Gate
endmodule
