// Logisim project debug.circ as structural Verilog: 1 circuit, main circuit main
module main (
  input  I0,
  input  I1
);

  wire and_1_out, and_2_out, and_3_out, and_4_out, not_1_out, not_2_out;

  not not_1 (not_1_out, I0);
  not not_2 (not_2_out, I1);
  and and_1 (and_1_out, not_1_out, not_2_out);
  and and_2 (and_2_out, not_2_out, I0);
  and and_3 (and_3_out, not_1_out, I1);
  and and_4 (and_4_out, I1, I0);
  _7_Segment_Display u_7_segment_display_1 (
    .g(and_1_out), .f(and_1_out), .e(and_1_out), .d(and_1_out));  // open: a, b, c, dp
  _7_Segment_Display u_7_segment_display_2 (
    .g(and_2_out), .f(and_2_out), .e(and_2_out), .c(and_2_out));  // open: a, b, d, dp
  _7_Segment_Display u_7_segment_display_3 (.b(and_3_out), .c(and_3_out));  // open: g, f, a, e, d, dp
  _7_Segment_Display u_7_segment_display_4 (.f(and_4_out), .a(and_4_out), .e(and_4_out));  // open: g, b, d, c, dp
endmodule
