// Logisim project rangkaian 1.circ as structural Verilog: 1 circuit, main circuit main
module main (
  input  A0,
  input  B0,
  input  A1,
  input  B1,
  output O0,
  output O1,
  output O2,
  output O3
);

  wire C1, P01, P10, P11;

  and P00 (O0, A0, B0);
  and u_P10 (P10, A1, B0);
  and u_P01 (P01, A0, B1);
  and u_P11 (P11, A1, B1);
  xor HA1 (O1, P10, P01);
  and u_C1 (C1, P10, P01);
  xor HA2 (O2, P11, C1);
  and and_1 (O3, P11, C1);

  // Other names for the same wires on the sheet: P00 = O0
endmodule
