// Logisim project rangkaian 2x2 bit.circ as structural Verilog: 1 circuit, main circuit main
module main (
  input  B1,
  input  B0,
  input  A1,
  input  A0,
  output OP3,
  output OP2,
  output OP1,
  output OP0
);

  wire AND_2_out, AND_3_out, AND_5_out, AND_out;

  and AND (AND_out, B1, A1);
  and AND_2 (AND_2_out, B1, A0);
  and AND_3 (AND_3_out, A1, B0);
  and AND_4 (OP0, B0, A0);
  xor XOR (OP1, AND_2_out, AND_3_out);
  and AND_5 (AND_5_out, AND_2_out, AND_3_out);
  xor XOR_2 (OP3, AND_out, AND_5_out);
  buf AND_6 (OP2, AND_out);  // AND_Gate

  // Notes on the sheet:
  //   ∑
  //   ∑
endmodule
