// Logisim project rangkaian Full Substractor.circ as structural Verilog: 1 circuit, main circuit main
module main (
  input  Bin,
  input  A1,
  input  B1,
  output out_4,
  output out_5
);

  wire and_1_out, and_2_out, not_1_out, not_2_out, xor_1_out;

  not not_1 (not_1_out, A1);
  xor xor_1 (xor_1_out, A1, B1);
  and and_1 (and_1_out, not_1_out, B1);
  xor xor_2 (out_4, Bin, xor_1_out);
  not not_2 (not_2_out, xor_1_out);
  and and_2 (and_2_out, not_2_out, Bin);
  or or_1 (out_5, and_2_out, and_1_out);
endmodule
