// Logisim project rangkaian Half Adder.circ as structural Verilog: 1 circuit, main circuit main
module main (
  input  A,
  input  B,
  output S,
  output C
);

  xor xor_1 (S, A, A);
  and and_1 (C, A, A);

  assign B = A;
endmodule
